# Fritzing sketch PotLight (saved by Fritzing 0.9.9b)
breadboards: 1

parts:
  Компонент1 = Arduino Uno (Rev3)
  R2 = Trimmer Potentiometer [maximum_resistance=10kΩ package=THT]
  R3 = Resistor [tolerance=±5% resistance=220 package=THT]
  LED1 = LED - 5mm [color="Red (633nm)" package="5 mm [THT]"]
  LED2 = LED - 5mm [color="Red (633nm)" package="5 mm [THT]"]
  R4 = Resistor [tolerance=±5% resistance=220 package=THT]

nets:
  N1: Компонент1.A0, R2.wiper
  N2: Компонент1.D9_PWM, R4.Pin_0
  N3: Компонент1.D5_PWM, R3.Pin_0
  N4: Компонент1.5V, R2.leg1
  N5: Компонент1.GND, R2.leg2, LED1.anode, LED2.anode
  N6: R3.Pin_1, LED1.cathode
  N7: LED2.cathode, R4.Pin_1
