# Fritzing sketch PulseLight (saved by Fritzing 0.9.9b)
breadboards: 1

parts:
  Компонент1 = Arduino Uno (Rev3)
  R1 = Resistor [tolerance=±5% resistance=220 package=THT]
  LED1 = LED - 5mm [color="Red (633nm)" package="5 mm [THT]"]
  LED2 = LED - 5mm [color="Red (633nm)" package="5 mm [THT]"]
  R2 = Resistor [tolerance=±5% resistance=220 package=THT]

nets:
  N1: Компонент1.D9_PWM, R1.Pin_1
  N2: Компонент1.D11_PWM/MOSI, R2.Pin_1
  N3: Компонент1.GND, LED1.cathode, LED2.cathode
  N4: R1.Pin_0, LED1.anode
  N5: LED2.anode, R2.Pin_0
